# Fritzing sketch COE (saved by Fritzing 0.9.2b)
breadboards: 3

parts:
  Part1 = Arduino Uno (Rev3)
  Part2 = Triple Axis Accelerometer Breakout - ADXL335
  LED1 = RGB LED - (4 legs) [package="5 mm [THT]"]
  LED2 = RGB LED - (4 legs) [package="5 mm [THT]"]
  LED3 = RGB LED - (4 legs) [package="5 mm [THT]"]
  LED4 = RGB LED - (4 legs) [package="5 mm [THT]"]
  LED5 = RGB LED - (4 legs) [package="5 mm [THT]"]
  LED6 = RGB LED - (4 legs) [package="5 mm [THT]"]
  LED7 = RGB LED - (4 legs) [package="5 mm [THT]"]
  LED8 = RGB LED - (4 legs) [package="5 mm [THT]"]
  S1 = Momentary Switch [package=ksa_sealed_tac_switch]
  S2 = Momentary Switch [package=ksa_sealed_tac_switch]
  R1 = Resistor [tolerance=±5% resistance=330 package="2010 [SMD]"]
  R2 = Resistor [tolerance=±5% resistance=330 package="2010 [SMD]"]
  R3 = Resistor [tolerance=±5% resistance=330 package="2010 [SMD]"]
  R4 = Resistor [tolerance=±5% resistance=330 package="2010 [SMD]"]
  R5 = Resistor [tolerance=±5% resistance=330 package="2010 [SMD]"]
  R6 = Resistor [tolerance=±5% resistance=330 package="2010 [SMD]"]
  R7 = Resistor [tolerance=±5% resistance=330 package="2010 [SMD]"]
  R8 = Resistor [tolerance=±5% resistance=330 package="2010 [SMD]"]
  R9 = Resistor [tolerance=±5% resistance=330 package="2010 [SMD]"]
  R10 = Resistor [tolerance=±5% resistance=330 package="2010 [SMD]"]
  R11 = Resistor [tolerance=±5% resistance=330 package="2010 [SMD]"]
  R14 = Resistor [tolerance=±5% resistance=330 package="2010 [SMD]"]
  R15 = Resistor [tolerance=±5% resistance=330 package="2010 [SMD]"]
  R16 = Resistor [tolerance=±5% resistance=330 package="2010 [SMD]"]
  R17 = Resistor [tolerance=±5% resistance=330 package="2010 [SMD]"]
  R18 = Resistor [tolerance=±5% resistance=330 package="2010 [SMD]"]
  R19 = Resistor [tolerance=±5% resistance=330 package="2010 [SMD]"]
  R20 = Resistor [tolerance=±5% resistance=330 package="2010 [SMD]"]
  R21 = Resistor [tolerance=±5% resistance=330 package="2010 [SMD]"]
  R22 = Resistor [tolerance=±5% resistance=330 package="2010 [SMD]"]
  R23 = Resistor [tolerance=±5% resistance=330 package="2010 [SMD]"]
  R24 = Resistor [tolerance=±5% resistance=330 package="2010 [SMD]"]
  R25 = Resistor [tolerance=±5% resistance=330 package="2010 [SMD]"]
  R26 = Resistor [tolerance=±5% resistance=330 package="2010 [SMD]"]
  R27 = Resistor [tolerance=±5% resistance=10k package="2512 [SMD]"]
  R28 = Resistor [tolerance=±5% resistance=10k package="2512 [SMD]"]
  C1 = Electrolytic Capacitor [capacitance=4.7µF package="200 mil [THT, electrolytic]"]
  Q1 = NPN-Transistor [part_number="NPN 3904" package="TO92 [THT]"]
  Q2 = NPN-Transistor [part_number="NPN 3904" package="TO92 [THT]"]
  Q3 = NPN-Transistor [part_number="NPN 3904" package="TO92 [THT]"]

nets:
  N1: Part1.A0, Part2.XOUT
  N2: Part1.A1, Part2.YOUT
  N3: Part1.A2, Part2.ZOUT, C1.+
  N4: Part1.D9_PWM, R2.Pin_1, R3.Pin_1, R9.Pin_1, R14.Pin_1, R17.Pin_1, R20.Pin_1, R23.Pin_1, Q2.B
  N5: Part1.D10_PWM/SS, Q3.B
  GND: Part1.GND, Part2.GND, S1.1, S2.1, C1.-, Q1.E, Q2.E, Q3.E
  N6: Part1.D2, S1.3
  N7: Part1.D3_PWM, Q1.B
  N8: Part1.D4, S2.3
  3V3: Part1.3V3, Part2.VCC
  N9: Part1.5V, LED1.common_anode, LED2.common_anode, LED3.common_anode, LED4.common_anode, LED5.common_anode, LED6.common_anode, LED7.common_anode, LED8.common_anode, R27.Pin_1, R28.Pin_1
  N10: LED1.red_cathode, R21.Pin_0
  N11: LED1.green_cathode, R20.Pin_0
  N12: LED1.blue_cathode, R19.Pin_0
  N13: LED2.red_cathode, R24.Pin_0
  N14: LED2.green_cathode, R23.Pin_0
  N15: LED2.blue_cathode, R22.Pin_0
  N16: LED3.red_cathode, R18.Pin_0
  N17: LED3.green_cathode, R17.Pin_0
  N18: LED3.blue_cathode, R16.Pin_0
  N19: LED4.red_cathode, R26.Pin_0
  N20: LED4.green_cathode, R25.Pin_0
  N21: LED4.blue_cathode, R6.Pin_0
  N22: LED5.red_cathode, R15.Pin_0
  N23: LED5.green_cathode, R14.Pin_0
  N24: LED5.blue_cathode, R1.Pin_0
  N25: LED6.red_cathode, R5.Pin_0
  N26: LED6.green_cathode, R2.Pin_0
  N27: LED6.blue_cathode, R10.Pin_0
  N28: LED7.red_cathode, R7.Pin_0
  N29: LED7.green_cathode, R3.Pin_0
  N30: LED7.blue_cathode, R11.Pin_0
  N31: LED8.red_cathode, R4.Pin_0
  N32: LED8.green_cathode, R9.Pin_0
  N33: LED8.blue_cathode, R8.Pin_0
  N34: S1.4, R28.Pin_0
  N35: S2.4, R27.Pin_0
  N36: R1.Pin_1, R6.Pin_1, R8.Pin_1, R10.Pin_1, R11.Pin_1, R16.Pin_1, R19.Pin_1, R22.Pin_1, Q3.C
  N37: R4.Pin_1, R5.Pin_1, R7.Pin_1, R15.Pin_1, R18.Pin_1, R21.Pin_1, R24.Pin_1, R26.Pin_1, Q1.C

// code stored in the sketch: fritz.ino

//Concepts of Engineering Arduino Demo


//Justin A. Barnes

//ENGR1402-002



//Analog input pins for accelerometer

const int xPin = 0; //pin Analog 0 (A0)

const int yPin = 1; //pin Analog 1 (A1)

const int zPin = 2; //pin Analog 2 (A2)



//LED Pins

const int redPin = 3;

const int greenPin = 9;

const int bluePin = 10;



//digital input Pins

const int potPin = 3; //pin Analog 3 (A3)

const int selectorPin = 2;

const int durationPin = 4;

const int resetPin = 5;

int resetState = 1;

int selectedPin = redPin;

int selectorState = 1;



//default values

int potValue = 0; //start from 255 as common anode, TF turned off

const int potLow = 4;    //These potentiometer values are derived by using a pot

const int potHigh = 820; //as a voltage divider and finding the low and high values

int accLow = 271;        //These accelerometer values are derived by rotating about

int accHigh = 405;       //the Z-axis to find the low and high output.

int xValue = 0;

int yValue = 0;          //Initially, set all these to off.

int zValue = 0;

int analogValue =0;

int pwmValue = 0;

int analogReadPin = zPin; //Start with Pot as input control



void setup() {  

  Serial.begin(9600);

  //Since we are using analogWrite on this pin, setting it to output is not needed

  //pinMode(bluePin,OUTPUT);

}



void loop() {

  selectorState = digitalRead(selectorPin);

  if(selectorState == LOW) 

  {

    //Switch LEDs

    if (selectedPin == redPin)

      selectedPin = greenPin;

    else if (selectedPin == greenPin)

      selectedPin = bluePin;

    else

      selectedPin = redPin;



    delay(500);

  }



  //Switch analog input pins

  resetState = digitalRead(resetPin);

  if (resetState == LOW)

  {

    if (analogReadPin == potPin)

      analogReadPin = zPin;

    else

      analogReadPin = potPin;



    delay(500);

  }



  //Read & map analog values to PWM values

  analogValue = analogRead(analogReadPin);



  if (analogReadPin == potPin)

  {

    pwmValue = map(analogValue,potLow,potHigh,0,255);

  }

  else

  {

    pwmValue = map(analogValue,accLow,accHigh,0,255);

  }



  //Roughly filter out overflow values on the PWM output

  if(pwmValue < 0)

    pwmValue = 0;

  if(pwmValue > 255)

    pwmValue = 255;



  analogWrite(selectedPin,pwmValue);

  

  //Serial.print("Button State:  ");

  //Serial.println(selectorState);

  //Serial.println(potValue);

  // delay(200);



  //  if (zValue < accLow)

  //    accLow = zValue;

  //

  //  if (zValue > accHigh)

  //    accHigh = zValue;



    Serial.print("Raw Pot:   ");

    Serial.print(analogRead(potPin));

    Serial.print("  accLow:  ");

    Serial.print(potLow);

    Serial.print("  accHigh:  ");

    Serial.print(potHigh);

    Serial.print("  pwm Value:  ");

    Serial.println(potValue);

 

}
